# Fritzing sketch LCD12864_8bit (saved by Fritzing 0.9.2b)
breadboards: 1

parts:
  元件1 = Arduino Uno (Rev3)
  GLCD_128x1 = 128 x 64 Graphic LCD

nets:
  N1: 元件1.A2, GLCD_128x1.5_R/W
  N2: 元件1.A3, GLCD_128x1.4_D/I
  N3: 元件1.A4/SDA, GLCD_128x1.6_Enable
  N4: 元件1.D8, GLCD_128x1.11_DB4
  N5: 元件1.D9_PWM, GLCD_128x1.12_DB5
  N6: 元件1.D10_PWM/SS, GLCD_128x1.13_DB6
  N7: 元件1.D11_PWM/MOSI, GLCD_128x1.14_DB7
  N8: 元件1.GND, GLCD_128x1.1_Vss, GLCD_128x1.20_K(-)
  N9: 元件1.D4, GLCD_128x1.7_DB0
  N10: 元件1.D5_PWM, GLCD_128x1.8_DB1
  N11: 元件1.D6_PWM, GLCD_128x1.9_BD2
  N12: 元件1.D7, GLCD_128x1.10_DB3
  N13: 元件1.5V, GLCD_128x1.2_Vdd, GLCD_128x1.15_CS1, GLCD_128x1.19_A(+)
