# Fritzing sketch LCD12864_spi (saved by Fritzing 0.9.2b)
breadboards: 1

parts:
  GLCD_128x1 = 128 x 64 Graphic LCD
  元件1 = Arduino Uno (Rev3)

nets:
  N1: GLCD_128x1.1_Vss, GLCD_128x1.15_CS1, GLCD_128x1.20_K(-), 元件1.GND
  N2: GLCD_128x1.2_Vdd, GLCD_128x1.19_A(+), 元件1.5V
  N3: GLCD_128x1.4_D/I, 元件1.D8
  N4: GLCD_128x1.5_R/W, 元件1.D9_PWM
  N5: GLCD_128x1.6_Enable, 元件1.D3_PWM
